# Fritzing sketch transmitter (saved by Fritzing 0.9.1b)
breadboards: 1

parts:
  U1 = RF-LINK_TX [package=rf-link_tx]  # not connected
  Part2 = SRF05 Ultrasonic Rangefinder
  Part3 = SRF05 Ultrasonic Rangefinder
  Part1 = Arduino Uno (Rev3)

nets:
  N1: Part2.Trig, Part1.D10_PWM/SS
  N2: Part2.Echo, Part1.D9_PWM
  N3: Part3.Trig, Part1.D8
  N4: Part3.Echo, Part1.D7
